// Logisim project ETFStudent.circ as structural Verilog: 7 circuits, main circuit REG32_LD
module REG32_LD (
  input  [31:0] I15__0,
  input  LD,
  input  mr,
  input  CLK,
  output [31:0] A15__0
);

  // REG16_LD reg16_ld_1: pin names not known; wires that end beside it: CLK, mr, I15__0[31:16], A15__0[31:16], LD
  // REG16_LD reg16_ld_2: pin names not known; wires that end beside it: CLK, mr, I15__0[15:0], A15__0[15:0], LD

  // Notes on the sheet:
  //   __
endmodule

module KMADR (
  input  immed,
  input  memdir,
  input  regdir,
  input  memind,
  input  postincr,
  input  pcrelpom,
  output [4:0] Adr3__0
);

  assign Adr3__0 = immed ? 5'b00010 : 5'bz;  // Controlled_Buffer controlled_buffer_1
  assign Adr3__0 = memdir ? 5'b00011 : 5'bz;  // Controlled_Buffer controlled_buffer_2
  assign Adr3__0 = regdir ? 5'b00100 : 5'bz;  // Controlled_Buffer controlled_buffer_3
  assign Adr3__0 = memind ? 5'b00110 : 5'bz;  // Controlled_Buffer controlled_buffer_4
  assign Adr3__0 = postincr ? 5'b01101 : 5'bz;  // Controlled_Buffer controlled_buffer_5
  assign Adr3__0 = pcrelpom ? 5'b10001 : 5'bz;  // Controlled_Buffer controlled_buffer_6
endmodule

module KMOPR (
  input  BLSS,
  input  BNCR,
  input  BGRTU,
  input  BNEG,
  input  LD,
  input  ST,
  input  SUB,
  input  AND,
  input  NOT,
  input  JLEQ,
  input  LOOPGRE,
  input  JMP,
  input  JSR,
  input  ASL,
  input  ROLC,
  input  RTS,
  input  RTI,
  input  PUSHGPR,
  input  POPGPR,
  input  HALT,
  output [6:0] Adr6__0
);

  wire or_1_out;

  assign Adr6__0 = LD ? 7'b0000010 : 7'bz;  // Controlled_Buffer controlled_buffer_1
  assign Adr6__0 = ST ? 7'b0000100 : 7'bz;  // Controlled_Buffer controlled_buffer_2
  assign Adr6__0 = SUB ? 7'b0001100 : 7'bz;  // Controlled_Buffer controlled_buffer_3
  assign Adr6__0 = AND ? 7'b0001110 : 7'bz;  // Controlled_Buffer controlled_buffer_4
  or or_1 (or_1_out, BLSS, BNCR, BGRTU, BNEG);
  assign Adr6__0 = NOT ? 7'b0010000 : 7'bz;  // Controlled_Buffer controlled_buffer_5
  assign Adr6__0 = or_1_out ? 7'b0010010 : 7'bz;  // Controlled_Buffer controlled_buffer_6
  assign Adr6__0 = JLEQ ? 7'b0010100 : 7'bz;  // Controlled_Buffer controlled_buffer_7
  assign Adr6__0 = LOOPGRE ? 7'b0010110 : 7'bz;  // Controlled_Buffer controlled_buffer_8
  assign Adr6__0 = JMP ? 7'b0011011 : 7'bz;  // Controlled_Buffer controlled_buffer_9
  assign Adr6__0 = JSR ? 7'b0011100 : 7'bz;  // Controlled_Buffer controlled_buffer_10
  assign Adr6__0 = ASL ? 7'b0100101 : 7'bz;  // Controlled_Buffer controlled_buffer_11
  assign Adr6__0 = ROLC ? 7'b0100101 : 7'bz;  // Controlled_Buffer controlled_buffer_12
  assign Adr6__0 = RTS ? 7'b0101001 : 7'bz;  // Controlled_Buffer controlled_buffer_13
  assign Adr6__0 = RTI ? 7'b0101111 : 7'bz;  // Controlled_Buffer controlled_buffer_14
  assign Adr6__0 = PUSHGPR ? 7'b0111100 : 7'bz;  // Controlled_Buffer controlled_buffer_15
  assign Adr6__0 = POPGPR ? 7'b1000111 : 7'bz;  // Controlled_Buffer controlled_buffer_16
  assign Adr6__0 = HALT ? 7'b1010000 : 7'bz;  // Controlled_Buffer controlled_buffer_17
endmodule

module REG6_INC_LD (
  input  [5:0] I5__0,
  input  LD,
  input  INC,
  input  mr,
  input  CLK,
  output [5:0] A5__0
);

  wire reg2m_inc_ld_1_p7, reg2m_inc_ld_2_p8;

  // REG2m_INC_LD reg2m_inc_ld_1: pin names not known; wires that end beside it: CLK, mr, I5__0[5:4], A5__0[5:4], LD, INC, reg2m_inc_ld_1_p7
  // REG2m_INC_LD reg2m_inc_ld_2: pin names not known; wires that end beside it: CLK, reg2m_inc_ld_1_p7, mr, I5__0[3:2], A5__0[3:2], LD, INC, reg2m_inc_ld_2_p8
  // REG2m_INC_LD reg2m_inc_ld_3: pin names not known; wires that end beside it: CLK, reg2m_inc_ld_2_p8, mr, I5__0[1:0], A5__0[1:0], LD, INC, INC

  // Notes on the sheet:
  //   __
endmodule

module ROM32x24 (
  input  [4:0] A4__0,
  input  CS,
  output [23:0] DOUT
);

  ROM #(.addrWidth(5), .dataWidth(24)) rom_1 (.addr(A4__0), .data(DOUT), .sel(CS));
endmodule

module GPR16x16 (
  input  [15:0] DI15__0,
  input  [3:0] A3__0,
  input  WR,
  input  CLK,
  input  INC,
  input  DEC,
  input  rst,
  output [15:0] DO15__0
);

  wire and_17_out, and_18_out, and_19_out, and_20_out, and_21_out, and_22_out, and_23_out, and_24_out,
       and_25_out, and_28_out, and_43_out, and_44_out, and_45_out, and_46_out, and_47_out, and_48_out, CS0,
       CS1, CS2, CS3, CS4, CS5, CS6, CS7, CS8, CS9, CS10, CS11, CS12, CS13, CS14, CS15, mp2_16b_1_p3,
       mp2_16b_2_p3, mp2_16b_3_p3, mp2_16b_4_p3, mp2_16b_5_p3, mp2_16b_6_p3, mp2_16b_7_p3, mp2_16b_8_p3,
       mp2_16b_9_p3, mp2_16b_10_p3, mp2_16b_11_p3, mp2_16b_12_p3, mp2_16b_13_p3, mp2_16b_14_p3,
       mp2_16b_15_p3, mp2_16b_16_p3, reg16_1_p4, reg16_1_p5, reg16_1_p6, reg16_2_p3, reg16_2_p4, reg16_2_p5,
       reg16_3_p4, reg16_3_p5, reg16_3_p6, reg16_4_p4, reg16_4_p5, reg16_4_p6, reg16_5_p4, reg16_5_p5,
       reg16_5_p6, reg16_6_p4, reg16_6_p5, reg16_6_p6, reg16_7_p3, reg16_7_p4, reg16_7_p5, reg16_8_p4,
       reg16_8_p5, reg16_8_p6, reg16_9_p4, reg16_9_p5, reg16_9_p6, reg16_10_p4, reg16_10_p5, reg16_10_p6,
       reg16_11_p4, reg16_11_p5, reg16_11_p6, reg16_12_p4, reg16_12_p5, reg16_12_p6, reg16_13_p4,
       reg16_13_p5, reg16_13_p6, reg16_14_p3, reg16_14_p4, reg16_14_p5, reg16_15_p4, reg16_15_p5,
       reg16_15_p6, reg16_16_p4, reg16_16_p5, reg16_16_p6;
  wire [15:0] reg16_1_p3, reg16_2_p2, reg16_3_p3, reg16_4_p3, reg16_5_p3, reg16_6_p3, reg16_7_p2, reg16_8_p3,
       reg16_9_p3, reg16_10_p3, reg16_11_p3, reg16_12_p3, reg16_13_p3, reg16_14_p2, reg16_15_p3, reg16_16_p3;

  // DC4_16 dc4_16_1: pin names not known; wires that end beside it: A3__0, 1'b1, CS0, CS1, CS2, CS3, CS4, CS5, CS6, CS7, CS8, CS9, CS10, CS11, CS12, CS13, CS14, CS15
  // MP2_16b mp2_16b_1: pin names not known; wires that end beside it: rst, DI15__0, mp2_16b_1_p3, {16{1'b0}}, 1'b1
  // REG16 reg16_1: pin names not known; wires that end beside it: CLK, mp2_16b_1_p3, reg16_1_p3, reg16_1_p4, reg16_1_p5, reg16_1_p6
  assign DO15__0 = CS0 ? reg16_1_p3 : 16'bz;  // Controlled_Buffer controlled_buffer_1
  // MP2_16b mp2_16b_2: pin names not known; wires that end beside it: rst, DI15__0, mp2_16b_2_p3, mp2_16b_2_p3, 16'hf000, 1'b1
  // REG16 reg16_2: pin names not known; wires that end beside it: CLK, reg16_2_p2, reg16_2_p3, reg16_2_p4, reg16_2_p5
  assign DO15__0 = CS1 ? reg16_2_p2 : 16'bz;  // Controlled_Buffer controlled_buffer_2
  // MP2_16b mp2_16b_3: pin names not known; wires that end beside it: rst, DI15__0, mp2_16b_3_p3, 16'h1000, 1'b1
  // REG16 reg16_3: pin names not known; wires that end beside it: CLK, mp2_16b_3_p3, reg16_3_p3, reg16_3_p4, reg16_3_p5, reg16_3_p6
  assign DO15__0 = CS2 ? reg16_3_p3 : 16'bz;  // Controlled_Buffer controlled_buffer_3
  // MP2_16b mp2_16b_4: pin names not known; wires that end beside it: rst, DI15__0, mp2_16b_4_p3, 16'h19a, 1'b1
  // REG16 reg16_4: pin names not known; wires that end beside it: CLK, mp2_16b_4_p3, reg16_4_p3, reg16_4_p4, reg16_4_p5, reg16_4_p6
  assign DO15__0 = CS3 ? reg16_4_p3 : 16'bz;  // Controlled_Buffer controlled_buffer_4
  // MP2_16b mp2_16b_5: pin names not known; wires that end beside it: rst, DI15__0, mp2_16b_5_p3, 16'hf512, 1'b1
  // REG16 reg16_5: pin names not known; wires that end beside it: CLK, mp2_16b_5_p3, reg16_5_p3, reg16_5_p4, reg16_5_p5, reg16_5_p6
  assign DO15__0 = CS4 ? reg16_5_p3 : 16'bz;  // Controlled_Buffer controlled_buffer_5
  // MP2_16b mp2_16b_6: pin names not known; wires that end beside it: rst, DI15__0, mp2_16b_6_p3, {16{1'b0}}, 1'b1
  // REG16 reg16_6: pin names not known; wires that end beside it: CLK, mp2_16b_6_p3, reg16_6_p3, reg16_6_p4, reg16_6_p5, reg16_6_p6
  assign DO15__0 = CS5 ? reg16_6_p3 : 16'bz;  // Controlled_Buffer controlled_buffer_6
  // MP2_16b mp2_16b_7: pin names not known; wires that end beside it: rst, DI15__0, mp2_16b_7_p3, mp2_16b_7_p3, {16{1'b0}}, 1'b1
  // REG16 reg16_7: pin names not known; wires that end beside it: CLK, reg16_7_p2, reg16_7_p3, reg16_7_p4, reg16_7_p5
  assign DO15__0 = CS6 ? reg16_7_p2 : 16'bz;  // Controlled_Buffer controlled_buffer_7
  // MP2_16b mp2_16b_8: pin names not known; wires that end beside it: rst, DI15__0, mp2_16b_8_p3, {16{1'b0}}, 1'b1
  // REG16 reg16_8: pin names not known; wires that end beside it: CLK, mp2_16b_8_p3, reg16_8_p3, reg16_8_p4, reg16_8_p5, reg16_8_p6
  assign DO15__0 = CS7 ? reg16_8_p3 : 16'bz;  // Controlled_Buffer controlled_buffer_8
  or or_1 (reg16_1_p4, and_17_out, rst);
  and and_1 (reg16_1_p5, CS0, INC);
  and and_2 (reg16_1_p6, CS0, DEC);
  or or_2 (reg16_2_p3, and_18_out, rst);
  and and_3 (reg16_2_p4, CS1, INC);
  and and_4 (reg16_2_p5, CS1, DEC);
  or or_3 (reg16_3_p4, and_19_out, rst);
  and and_5 (reg16_3_p5, CS2, INC);
  and and_6 (reg16_3_p6, CS2, DEC);
  or or_4 (reg16_4_p4, and_20_out, rst);
  and and_7 (reg16_4_p5, CS3, INC);
  and and_8 (reg16_4_p6, CS3, DEC);
  or or_5 (reg16_5_p4, and_21_out, rst);
  and and_9 (reg16_5_p5, CS4, INC);
  and and_10 (reg16_5_p6, CS4, DEC);
  or or_6 (reg16_6_p4, and_22_out, rst);
  and and_11 (reg16_6_p5, CS5, INC);
  and and_12 (reg16_6_p6, CS5, DEC);
  or or_7 (reg16_7_p3, and_23_out, rst);
  and and_13 (reg16_7_p4, CS6, INC);
  and and_14 (reg16_7_p5, CS6, DEC);
  or or_8 (reg16_8_p4, and_24_out, rst);
  and and_15 (reg16_8_p5, CS7, INC);
  and and_16 (reg16_8_p6, CS7, DEC);
  and and_17 (and_17_out, CS0, WR);
  and and_18 (and_18_out, CS1, WR);
  and and_19 (and_19_out, CS2, WR);
  and and_20 (and_20_out, CS3, WR);
  and and_21 (and_21_out, CS4, WR);
  and and_22 (and_22_out, CS5, WR);
  and and_23 (and_23_out, CS6, WR);
  and and_24 (and_24_out, CS7, WR);
  // MP2_16b mp2_16b_9: pin names not known; wires that end beside it: rst, DI15__0, mp2_16b_9_p3, {16{1'b0}}, 1'b1
  // REG16 reg16_9: pin names not known; wires that end beside it: CLK, mp2_16b_9_p3, reg16_9_p3, reg16_9_p4, reg16_9_p5, reg16_9_p6
  assign DO15__0 = CS8 ? reg16_9_p3 : 16'bz;  // Controlled_Buffer controlled_buffer_9
  // MP2_16b mp2_16b_10: pin names not known; wires that end beside it: rst, DI15__0, mp2_16b_10_p3, {16{1'b0}}, 1'b1
  // REG16 reg16_10: pin names not known; wires that end beside it: CLK, mp2_16b_10_p3, reg16_10_p3, reg16_10_p4, reg16_10_p5, reg16_10_p6
  assign DO15__0 = CS9 ? reg16_10_p3 : 16'bz;  // Controlled_Buffer controlled_buffer_10
  // MP2_16b mp2_16b_11: pin names not known; wires that end beside it: rst, DI15__0, mp2_16b_11_p3, {16{1'b0}}, 1'b1
  // REG16 reg16_11: pin names not known; wires that end beside it: CLK, mp2_16b_11_p3, reg16_11_p3, reg16_11_p4, reg16_11_p5, reg16_11_p6
  assign DO15__0 = CS10 ? reg16_11_p3 : 16'bz;  // Controlled_Buffer controlled_buffer_11
  // MP2_16b mp2_16b_12: pin names not known; wires that end beside it: rst, DI15__0, mp2_16b_12_p3, {16{1'b0}}, 1'b1
  // REG16 reg16_12: pin names not known; wires that end beside it: CLK, mp2_16b_12_p3, reg16_12_p3, reg16_12_p4, reg16_12_p5, reg16_12_p6
  assign DO15__0 = CS11 ? reg16_12_p3 : 16'bz;  // Controlled_Buffer controlled_buffer_12
  // MP2_16b mp2_16b_13: pin names not known; wires that end beside it: rst, DI15__0, mp2_16b_13_p3, {16{1'b0}}, 1'b1
  // REG16 reg16_13: pin names not known; wires that end beside it: CLK, mp2_16b_13_p3, reg16_13_p3, reg16_13_p4, reg16_13_p5, reg16_13_p6
  assign DO15__0 = CS12 ? reg16_13_p3 : 16'bz;  // Controlled_Buffer controlled_buffer_13
  // MP2_16b mp2_16b_14: pin names not known; wires that end beside it: rst, DI15__0, mp2_16b_14_p3, mp2_16b_14_p3, {16{1'b0}}, 1'b1
  // REG16 reg16_14: pin names not known; wires that end beside it: CLK, reg16_14_p2, reg16_14_p3, reg16_14_p4, reg16_14_p5
  assign DO15__0 = CS13 ? reg16_14_p2 : 16'bz;  // Controlled_Buffer controlled_buffer_14
  // MP2_16b mp2_16b_15: pin names not known; wires that end beside it: rst, DI15__0, mp2_16b_15_p3, {16{1'b0}}, 1'b1
  // REG16 reg16_15: pin names not known; wires that end beside it: CLK, mp2_16b_15_p3, reg16_15_p3, reg16_15_p4, reg16_15_p5, reg16_15_p6
  assign DO15__0 = CS14 ? reg16_15_p3 : 16'bz;  // Controlled_Buffer controlled_buffer_15
  // MP2_16b mp2_16b_16: pin names not known; wires that end beside it: rst, DI15__0, mp2_16b_16_p3, {16{1'b0}}, 1'b1
  // REG16 reg16_16: pin names not known; wires that end beside it: CLK, mp2_16b_16_p3, reg16_16_p3, reg16_16_p4, reg16_16_p5, reg16_16_p6
  assign DO15__0 = CS15 ? reg16_16_p3 : 16'bz;  // Controlled_Buffer controlled_buffer_16
  and and_25 (and_25_out, CS8, WR);
  or or_9 (reg16_9_p4, and_25_out, rst);
  and and_26 (reg16_9_p5, CS8, INC);
  and and_27 (reg16_9_p6, CS8, DEC);
  and and_28 (and_28_out, CS9, WR);
  or or_10 (reg16_10_p4, and_28_out, rst);
  and and_29 (reg16_10_p5, CS9, INC);
  and and_30 (reg16_10_p6, CS9, DEC);
  or or_11 (reg16_11_p4, and_43_out, rst);
  and and_31 (reg16_11_p5, CS10, INC);
  and and_32 (reg16_11_p6, CS10, DEC);
  or or_12 (reg16_12_p4, and_44_out, rst);
  and and_33 (reg16_12_p5, CS11, INC);
  and and_34 (reg16_12_p6, CS11, DEC);
  or or_13 (reg16_13_p4, and_45_out, rst);
  and and_35 (reg16_13_p5, CS12, INC);
  and and_36 (reg16_13_p6, CS12, DEC);
  or or_14 (reg16_14_p3, and_46_out, rst);
  and and_37 (reg16_14_p4, CS13, INC);
  and and_38 (reg16_14_p5, CS13, DEC);
  or or_15 (reg16_15_p4, and_47_out, rst);
  and and_39 (reg16_15_p5, CS14, INC);
  and and_40 (reg16_15_p6, CS14, DEC);
  or or_16 (reg16_16_p4, and_48_out, rst);
  and and_41 (reg16_16_p5, CS15, INC);
  and and_42 (reg16_16_p6, CS15, DEC);
  and and_43 (and_43_out, CS10, WR);
  and and_44 (and_44_out, CS11, WR);
  and and_45 (and_45_out, CS12, WR);
  and and_46 (and_46_out, CS13, WR);
  and and_47 (and_47_out, CS14, WR);
  and and_48 (and_48_out, CS15, WR);

  // Other names for the same wires on the sheet: inREG[15:0] = DI15__0; outREG[15:0] = DO15__0
endmodule

module ALU_16_SUB_AND_NOT (
  input  cin,
  input  [15:0] A,
  input  [15:0] B,
  input  sub,
  input  \and ,
  input  \not ,
  output [15:0] F,
  output cout
);

  wire [15:0] and_1_out, not_1_out, subtractor_1_out;

  Subtractor #(.width(16)) subtractor_1 (.a(A), .b(B), .out(subtractor_1_out), .bin(cin), .bout(cout));
  assign and_1_out = A & B;  // AND_Gate and_1, 16 bits wide
  assign not_1_out = ~B;  // NOT_Gate not_1, 16 bits wide
  assign F = sub ? subtractor_1_out : 16'bz;  // Controlled_Buffer controlled_buffer_1
  assign F = \and  ? and_1_out : 16'bz;  // Controlled_Buffer controlled_buffer_2
  assign F = \not  ? not_1_out : 16'bz;  // Controlled_Buffer controlled_buffer_3
endmodule
