// Logisim project ORT2Project.circ as structural Verilog: 8 circuits, main circuit COMPUTER
module COMPUTER (
);

  wire BTN_RST_out, CLK, cpu_1_inta, interrupt_interface_4_1_p4, interrupt_interface_4_1_p5,
       interrupt_interface_4_1_p6, interrupt_interface_4_1_p7, pull_resistor_2_node, pull_resistor_5_node,
       ram_1_out_8, rst;
  wire [1:0] cpu_1_uext1__0;
  wire [3:0] interrupt_interface_4_1_p1;
  wire [7:0] pull_resistor_1_node, ram_1_out_7;
  wire [15:0] pull_resistor_4_node;

  Button BTN_RST (.out(BTN_RST_out));
  Clock u_CLK (.out(CLK));
  // RisingEdge risingedge_1: pin names not known; wires that end beside it: BTN_RST_out, CLK, rst
  RAM ram_1 (
    .in_1(pull_resistor_4_node), .in_2(CLK), .in_3(pull_resistor_1_node), .in_4(pull_resistor_2_node),
    .in_5(pull_resistor_5_node), .in_6(rst), .out_7(ram_1_out_7), .out_8(ram_1_out_8));
  Pull_Resistor pull_resistor_1 (.node(pull_resistor_1_node));
  Pull_Resistor pull_resistor_2 (.node(pull_resistor_2_node));
  Pull_Resistor pull_resistor_3 (.node(ram_1_out_7));
  Pull_Resistor pull_resistor_4 (.node(pull_resistor_4_node));
  Pull_Resistor pull_resistor_5 (.node(pull_resistor_5_node));
  Pull_Resistor pull_resistor_6 (.node(ram_1_out_8));
  CPU cpu_1 (
    .in_1(rst), .in_2(CLK), .in_3(ram_1_out_8), .in_4(ram_1_out_7), .ABUS(pull_resistor_4_node),
    .DOUTBUS(pull_resistor_1_node), .out_8(pull_resistor_2_node), .out_9(pull_resistor_5_node),
    .inta(cpu_1_inta), .intr3__0(interrupt_interface_4_1_p1), .UEXT1__0(cpu_1_uext1__0));
  // INTERRUPT_INTERFACE_4 interrupt_interface_4_1: pin names not known; wires that end beside it: interrupt_interface_4_1_p1, cpu_1_inta, cpu_1_uext1__0, interrupt_interface_4_1_p4, interrupt_interface_4_1_p5, interrupt_interface_4_1_p6, interrupt_interface_4_1_p7, CLK
  Button BTN_INTR3 (.out(interrupt_interface_4_1_p4));
  Button BTN_INTR2 (.out(interrupt_interface_4_1_p5));
  Button BTN_INTR1 (.out(interrupt_interface_4_1_p6));
  Button BTN_INTR0 (.out(interrupt_interface_4_1_p7));
endmodule

module CPU (
  input  in_1,
  input  in_2,
  input  in_3,
  input  [7:0] in_4,
  input  [3:0] intr3__0,
  output [15:0] ABUS,
  output [7:0] DOUTBUS,
  output out_8,
  output out_9,
  output inta,
  output [1:0] UEXT1__0
);

  wire [3:0] common_1_phaseffbus;
  wire [5:0] common_1_addrbus;
  wire [6:0] pull_resistor_2_node;
  wire [7:0] A, ALU, pull_resistor_6_node;
  wire [14:0] pull_resistor_5_node;
  wire [15:0] B, INTRADDR, PSW;
  wire [19:0] common_1_instrucbus;
  wire [23:0] pull_resistor_7_node;

  COMMON common_1 (
    .CLK(in_2), .RST(in_1), .DIN(in_4), .CMEMBUS(pull_resistor_5_node), .MAR(ABUS), .MDR(DOUTBUS),
    .PHASEFFBUS(common_1_phaseffbus), .INSTRUCBUS(common_1_instrucbus), .ADDRBUS(common_1_addrbus),
    .PSW(PSW), .CFFBUS(pull_resistor_6_node), .B(B), .A(A), .CPSW(pull_resistor_2_node), .ALU(ALU),
    .IVTPPDSP(INTRADDR), .CREGBUS(pull_resistor_7_node));
  Pull_Resistor pull_resistor_1 (.node(common_1_phaseffbus));
  Pull_Resistor pull_resistor_2 (.node(pull_resistor_2_node));
  Pull_Resistor pull_resistor_3 (.node(common_1_instrucbus));
  Pull_Resistor pull_resistor_4 (.node(common_1_addrbus));
  Pull_Resistor pull_resistor_5 (.node(pull_resistor_5_node));
  Pull_Resistor pull_resistor_6 (.node(pull_resistor_6_node));
  Pull_Resistor pull_resistor_7 (.node(pull_resistor_7_node));
  FETCH fetch_1 (
    .in_1(in_1), .in_2(in_2), .in_3(in_3), .PHASEFFBUS(common_1_phaseffbus),
    .INSTRUCBUS(common_1_instrucbus), .ADDRBUS(common_1_addrbus), .PSW(PSW), .rdMEM(out_9),
    .CMEMBUS(pull_resistor_5_node), .CFFBUS(pull_resistor_6_node), .CREGBUS(pull_resistor_7_node));
  ADDR addr_1 (
    .in_1(in_1), .in_2(in_2), .in_3(in_3), .PHASEFFBUS(common_1_phaseffbus),
    .INSTRUCBUS(common_1_instrucbus), .ADDRBUS(common_1_addrbus), .rdMEM(out_9),
    .CMEMBUS(pull_resistor_5_node), .CFFBUS(pull_resistor_6_node), .CREGBUS(pull_resistor_7_node));
  EXEC exec_1 (
    .in_1(in_1), .in_2(in_2), .in_3(in_3), .B(B), .PHASEFFBUS(common_1_phaseffbus),
    .INSTRUCBUS(common_1_instrucbus), .ADDRBUS(common_1_addrbus), .PSW(PSW), .A(A), .ALU(ALU),
    .CMEMBUS(pull_resistor_5_node), .CFFBUS(pull_resistor_6_node), .CREGBUS(pull_resistor_7_node),
    .CPSW(pull_resistor_2_node), .rdMEM(out_9), .wrMEM(out_8));
  INTR intr_1 (
    .in_1(in_1), .in_2(in_2), .in_3(in_3), .PHASEFFBUS(common_1_phaseffbus),
    .INSTRUCBUS(common_1_instrucbus), .PSW(PSW), .intr(intr3__0), .ADDIVTP(INTRADDR),
    .CMEMBUS(pull_resistor_5_node), .CFFBUS(pull_resistor_6_node), .CREGBUS(pull_resistor_7_node),
    .rdMEM(out_9), .wrMEM(out_8), .UEXT1__0(UEXT1__0), .inta(inta));

  // Other names for the same wires on the sheet: CLK = in_2; DIN7__0[7:0] = in_4; FCBUS = in_3; MAR[15:0] = ABUS;
  //   MDR[7:0] = DOUTBUS; RD = out_9; rst = in_1; WR = out_8
endmodule

module COMMON (
  input  CLK,
  input  RST,
  input  [7:0] DIN,
  input  [7:0] A,
  input  [7:0] ALU,
  input  [15:0] IVTPPDSP,
  input  [14:0] CMEMBUS,
  input  [7:0] CFFBUS,
  input  [23:0] CREGBUS,
  input  [6:0] CPSW,
  output [15:0] MAR,
  output [7:0] MDR,
  output [3:0] PHASEFFBUS,
  output [19:0] INSTRUCBUS,
  output [5:0] ADDRBUS,
  output [15:0] PSW,
  output [15:0] B
);

  wire ACCZN, adrinst, ALU15, and_2_out, and_3_out, and_4_out, and_5_out, and_6_out, and_7_out, and_8_out,
       and_9_out, and_10_out, and_11_out, and_12_out, and_13_out, and_14_out, and_15_out, and_16_out,
       and_17_out, and_18_out, and_19_out, and_20_out, and_21_out, and_22_out, and_23_out, and_24_out,
       and_25_out, and_26_out, and_27_out, and_28_out, and_29_out, bezadrinst, BOUT, branchinst, COUT, DW0,
       DW1, DW2, DW3, DW4, DW15, GPR15, jmpinst, mp4_16b_1_p5, mp4_16b_1_p7, mp8_8b_1_p8, mp8_16b_1_p8,
       not_1_out, not_4_out, or_1_out, or_2_out, or_3_out, or_4_out, or_5_out, or_6_out, or_7_out, or_8_out,
       or_10_out, or_11_out, reg16_1_p6, reg16_1_p7, rsff_2_p4, rsff_3_p4, rsff_5_p4, rsff_6_p4, rsff_7_p4,
       rsff_8_p4, rsff_9_p4, rsff_10_p4;
  wire [3:0] mp8_4b_1_p8;
  wire [6:0] DWH;
  wire [7:0] IR7__0, IR15__8, IR23__16, IR31__24;
  wire [7:5] DWL;
  wire [14:0] ALU15__0, GPR15__0;
  wire [15:0] ADDPCREL15__0, BRANCH15__0, mp8_16b_2_p8;

  ALU_16_SUB_AND_NOT alu_16_sub_and_not_1 (
    .cin(1'b0), .A({GPR15, GPR15__0}), .B(B), .sub(CREGBUS[20]), .\and (CREGBUS[21]), .\not (CREGBUS[19]),
    .F({ALU15, ALU15__0}), .cout(COUT));
  // MP8_16b mp8_16b_1: pin names not known; wires that end beside it: CMEMBUS[7], CMEMBUS[6], CMEMBUS[5], {GPR15, GPR15__0}, {IR7__0, IR15__8}, ADDPCREL15__0, B, mp8_16b_1_p8, IVTPPDSP, 1'b1
  // REG16_INC_LD reg16_inc_ld_1: pin names not known; wires that end beside it: CLK, mp8_16b_1_p8, MAR, CMEMBUS[0], CMEMBUS[1]
  // DC2_4 dc2_4_1: pin names not known; wires that end beside it: IR31__24[5:4], PSW[0], bezadrinst, branchinst, jmpinst, adrinst
  // DC3_8 dc3_8_1: pin names not known; wires that end beside it: IR31__24[2:0], bezadrinst, INSTRUCBUS[0], INSTRUCBUS[1], INSTRUCBUS[2], INSTRUCBUS[3], INSTRUCBUS[4], INSTRUCBUS[5], INSTRUCBUS[6]
  // REG8_LD reg8_ld_1: pin names not known; wires that end beside it: CLK, MDR, IR31__24, CREGBUS[7]
  // REG8_LD reg8_ld_2: pin names not known; wires that end beside it: CLK, MDR, IR23__16, CREGBUS[6]
  // DC3_8 dc3_8_2: pin names not known; wires that end beside it: IR23__16[7:5], adrinst, ADDRBUS[0], ADDRBUS[1], ADDRBUS[2], ADDRBUS[3], ADDRBUS[4], ADDRBUS[5]
  // DC3_8 dc3_8_3: pin names not known; wires that end beside it: IR31__24[2:0], branchinst, INSTRUCBUS[7], INSTRUCBUS[8], INSTRUCBUS[9], INSTRUCBUS[10], INSTRUCBUS[11], INSTRUCBUS[12]
  // DC1_2 dc1_2_1: pin names not known; wires that end beside it: IR31__24[0], jmpinst, INSTRUCBUS[13], INSTRUCBUS[14]
  // DC3_8 dc3_8_4: pin names not known; wires that end beside it: IR31__24[2:0], adrinst, INSTRUCBUS[15], INSTRUCBUS[16], INSTRUCBUS[17], INSTRUCBUS[18], INSTRUCBUS[19]
  // MP8_8b mp8_8b_1: pin names not known; wires that end beside it: CMEMBUS[10], CMEMBUS[9], CMEMBUS[8], DIN, {GPR15, GPR15__0[14:8]}, GPR15__0[7:0], {PSW[15], {7{1'b0}}}, mp8_8b_1_p8, {3'b000, PSW[4:0]}, 1'b1
  // REG8_LD reg8_ld_3: pin names not known; wires that end beside it: CLK, mp8_8b_1_p8, MDR, CMEMBUS[2]
  // REG8_LD reg8_ld_4: pin names not known; wires that end beside it: CLK, MDR, IR15__8, CREGBUS[5]
  // REG8_LD reg8_ld_5: pin names not known; wires that end beside it: CLK, MDR, IR7__0, CREGBUS[4]
  // MP4_16b mp4_16b_1: pin names not known; wires that end beside it: CREGBUS[2], CREGBUS[1], {GPR15, GPR15__0}, {IR7__0, IR15__8}, mp4_16b_1_p5, {DW15, DWH, DWL, DW4, DW3, DW2, DW1, DW0}, mp4_16b_1_p7, 1'b1
  // REG16 reg16_1: pin names not known; wires that end beside it: BOUT, CLK, mp4_16b_1_p5, B, CREGBUS[0], reg16_1_p6, reg16_1_p7, CREGBUS[10], CREGBUS[17]
  // REG8_LD reg8_ld_6: pin names not known; wires that end beside it: CLK, MDR, {DW15, DWH}, CREGBUS[8]
  // REG8_LD reg8_ld_7: pin names not known; wires that end beside it: CLK, MDR, {DWL, DW4, DW3, DW2, DW1, DW0}, CREGBUS[9]
  not not_1 (not_1_out, RST);
  // RSFF rsff_1: pin names not known; wires that end beside it: CFFBUS[1], CLK, CFFBUS[0], not_1_out, PHASEFFBUS[0]
  or or_1 (or_1_out, INSTRUCBUS[3], INSTRUCBUS[4]);
  and and_1 (reg16_1_p6, or_1_out, CREGBUS[16]);
  // ADD16 add16_1: pin names not known; wires that end beside it: IR15__8[7], {{9{IR15__8[7]}}, IR15__8[6:0]}, ADDPCREL15__0, {GPR15, GPR15__0}
  // ADD16 add16_2: pin names not known; wires that end beside it: IR23__16[7], {{9{IR23__16[7]}}, IR23__16[6:0]}, BRANCH15__0, {GPR15, GPR15__0}
  // MP2_16b mp2_16b_1: pin names not known; wires that end beside it: INSTRUCBUS[6], {16{1'b0}}, mp4_16b_1_p7, 16'hf, 1'b1
  // MP2_1b mp2_1b_1: pin names not known; wires that end beside it: INSTRUCBUS[4], 1'b0, reg16_1_p7, PSW[4], 1'b1
  // RSFF rsff_2: pin names not known; wires that end beside it: CFFBUS[3], CLK, CFFBUS[2], rsff_2_p4, PHASEFFBUS[1]
  not not_2 (rsff_2_p4, RST);
  and and_2 (and_2_out, ~B[15], GPR15);  // AND_Gate
  and and_3 (and_3_out, ~ALU15, ~B[15], GPR15);  // AND_Gate
  and and_4 (and_4_out, ALU15, B[15], ~GPR15);  // AND_Gate
  and and_5 (and_5_out, INSTRUCBUS[12], BOUT);
  and and_6 (and_6_out, INSTRUCBUS[17], COUT);
  and and_7 (and_7_out, B[15], or_2_out);
  or or_2 (or_2_out, INSTRUCBUS[3], INSTRUCBUS[4]);
  // RSFF rsff_3: pin names not known; wires that end beside it: CFFBUS[5], CLK, CFFBUS[4], rsff_3_p4, PHASEFFBUS[2]
  not not_3 (rsff_3_p4, RST);
  and and_8 (and_8_out, ~DW0, CPSW[1], INSTRUCBUS[2]);  // AND_Gate
  and and_9 (and_9_out, DW0, CPSW[1], INSTRUCBUS[2]);
  and and_10 (and_10_out, ~GPR15__0[0], ~GPR15__0[1], ~GPR15__0[2], ~GPR15__0[3], ~GPR15__0[4], ~GPR15__0[5], ~GPR15__0[6], ~GPR15__0[7], ~GPR15__0[8], ~GPR15__0[9], ~GPR15__0[10], ~GPR15__0[11], ~GPR15__0[12], ~GPR15__0[13], ~GPR15__0[14], ~GPR15);  // AND_Gate
  or or_3 (or_3_out, and_3_out, and_4_out);
  or or_4 (or_4_out, and_8_out, CPSW[0]);
  and and_11 (and_11_out, INSTRUCBUS[2], DW1);
  and and_12 (and_12_out, ACCZN, and_10_out);
  and and_13 (and_13_out, INSTRUCBUS[2], DW2);
  and and_14 (and_14_out, ACCZN, GPR15);
  and and_15 (and_15_out, INSTRUCBUS[2], DW3);
  and and_16 (and_16_out, INSTRUCBUS[12], and_2_out);
  and and_17 (and_17_out, INSTRUCBUS[17], or_3_out);
  and and_18 (and_18_out, INSTRUCBUS[2], DW4);
  and and_19 (and_19_out, INSTRUCBUS[2], DW15);
  not not_4 (not_4_out, RST);
  // RSFF rsff_4: pin names not known; wires that end beside it: or_4_out, CLK, and_9_out, not_4_out, PSW[0]
  or or_5 (or_5_out, and_11_out, and_12_out);
  and and_20 (and_20_out, or_5_out, CPSW[2]);
  or or_6 (or_6_out, and_13_out, and_14_out);
  or or_7 (or_7_out, and_15_out, and_16_out, and_17_out);
  or or_8 (or_8_out, and_18_out, and_5_out, and_6_out, and_7_out);
  and and_21 (and_21_out, ~or_8_out, CPSW[5]);  // AND_Gate
  and and_22 (and_22_out, or_8_out, CPSW[5]);
  and and_23 (and_23_out, ~and_19_out, CPSW[6]);  // AND_Gate
  and and_24 (and_24_out, and_19_out, CPSW[6]);
  // RSFF rsff_5: pin names not known; wires that end beside it: CFFBUS[7], CLK, CFFBUS[6], rsff_5_p4, PHASEFFBUS[3]
  not not_5 (rsff_5_p4, RST);
  or or_9 (ACCZN, INSTRUCBUS[15], INSTRUCBUS[17], INSTRUCBUS[18], INSTRUCBUS[4], INSTRUCBUS[19], INSTRUCBUS[12], INSTRUCBUS[3]);
  and and_25 (and_25_out, ~or_5_out, CPSW[2]);  // AND_Gate
  and and_26 (and_26_out, ~or_6_out, CPSW[3]);  // AND_Gate
  and and_27 (and_27_out, or_6_out, CPSW[3]);
  and and_28 (and_28_out, ~or_7_out, CPSW[4]);  // AND_Gate
  and and_29 (and_29_out, or_7_out, CPSW[4]);
  // RSFF rsff_6: pin names not known; wires that end beside it: and_21_out, CLK, and_22_out, rsff_6_p4, PSW[4]
  not not_6 (rsff_6_p4, RST);
  // RSFF rsff_7: pin names not known; wires that end beside it: and_23_out, CLK, and_24_out, rsff_7_p4, PSW[15]
  not not_7 (rsff_7_p4, RST);
  // RSFF rsff_8: pin names not known; wires that end beside it: and_25_out, CLK, and_20_out, rsff_8_p4, PSW[1]
  not not_8 (rsff_8_p4, RST);
  // RSFF rsff_9: pin names not known; wires that end beside it: and_26_out, CLK, and_27_out, rsff_9_p4, PSW[2]
  not not_9 (rsff_9_p4, RST);
  // RSFF rsff_10: pin names not known; wires that end beside it: and_28_out, CLK, and_29_out, rsff_10_p4, PSW[3]
  not not_10 (rsff_10_p4, RST);
  // MP8_4b mp8_4b_1: pin names not known; wires that end beside it: CREGBUS[18], CREGBUS[12], CREGBUS[11], 4'b0010, IR23__16[3:0], 4'b0001, 4'b0000, mp8_4b_1_p8, B[3:0]
  GPR16x16 gpr16x16_1 (
    .DI15__0(mp8_16b_2_p8), .A3__0(mp8_4b_1_p8), .WR(or_11_out), .CLK(CLK), .INC(or_10_out),
    .DEC(CMEMBUS[12]), .rst(RST), .DO15__0({GPR15, GPR15__0}));
  // MP8_16b mp8_16b_2: pin names not known; wires that end beside it: CREGBUS[15], CREGBUS[14], CREGBUS[13], B, BRANCH15__0, {IR15__8, IR23__16}, {DW15, DWH, DWL, DW4, DW3, DW2, DW1, DW0}, mp8_16b_2_p8, {ALU15, ALU15__0}
  or or_10 (or_10_out, CMEMBUS[4], CMEMBUS[11]);
  or or_11 (or_11_out, CREGBUS[3], CMEMBUS[3]);

  assign PSW[14:5] = {10{1'b0}};

  // Other names for the same wires on the sheet: DWL[4:0] = {DW4, DW3, DW2, DW1, DW0}; DWH[7] = DW15; A7__0[7:0] = A;
  //   immed = ADDRBUS[0]; memdir = ADDRBUS[1]; regdir = ADDRBUS[2]; memind = ADDRBUS[3]; postincr = ADDRBUS[4];
  //   pcrelpom = ADDRBUS[5]; ALU7__0[7:0] = ALU; ALU15__0[15] = ALU15; B3__0[3:0] = B[3:0]; B15__0[15:0] = B;
  //   stFETCH = CFFBUS[0]; clFETCH = CFFBUS[1]; stADDR = CFFBUS[2]; clADDR = CFFBUS[3]; stEXEC = CFFBUS[4];
  //   clEXEC = CFFBUS[5]; stINTR = CFFBUS[6]; clINTR = CFFBUS[7]; ldMAR = CMEMBUS[0]; incMAR = CMEMBUS[1];
  //   ldMDR = CMEMBUS[2]; ldPC = CMEMBUS[3]; incPC = CMEMBUS[4]; mxMAR0 = CMEMBUS[5]; mxMAR1 = CMEMBUS[6];
  //   mxMAR2 = CMEMBUS[7]; mxMDR0 = CMEMBUS[8]; mxMDR1 = CMEMBUS[9]; mxMDR2 = CMEMBUS[10]; incSP = CMEMBUS[11];
  //   decSP = CMEMBUS[12]; clPSWSTART = CPSW[0]; ldSTART = CPSW[1]; ldZ = CPSW[2]; ldN = CPSW[3]; ldV = CPSW[4];
  //   ldC = CPSW[5]; ldI = CPSW[6]; ldB = CREGBUS[0]; mxB0 = CREGBUS[1]; mxB1 = CREGBUS[2]; wrGPR = CREGBUS[3];
  //   ldIR7__0 = CREGBUS[4]; ldIR15__8 = CREGBUS[5]; ldIR23__16 = CREGBUS[6]; ldIR31__24 = CREGBUS[7];
  //   ldDWH = CREGBUS[8]; ldDWL = CREGBUS[9]; incB = CREGBUS[10]; mxGPRADR0 = CREGBUS[11]; mxGPRADR1 = CREGBUS[12];
  //   mxGPRIN0 = CREGBUS[13]; mxGPRIN1 = CREGBUS[14]; mxGPRIN2 = CREGBUS[15]; slB = CREGBUS[16]; decB = CREGBUS[17];
  //   mxGPRADR2 = CREGBUS[18]; NOTALU = CREGBUS[19]; SUBALU = CREGBUS[20]; ANDALU = CREGBUS[21]; Din7__0[7:0] = DIN;
  //   ENTRADDR15__0[15:0] = IVTPPDSP; GPR15__0[15] = GPR15; HALT = INSTRUCBUS[0]; RTS = INSTRUCBUS[1];
  //   RTI = INSTRUCBUS[2]; ASL = INSTRUCBUS[3]; ROLC = INSTRUCBUS[4]; PUSHGPR = INSTRUCBUS[5]; POPGPR = INSTRUCBUS[6];
  //   BLSS = INSTRUCBUS[7]; BNCR = INSTRUCBUS[8]; BGRTU = INSTRUCBUS[9]; BNEG = INSTRUCBUS[10]; JLEQ = INSTRUCBUS[11];
  //   LOOPGRE = INSTRUCBUS[12]; JMP = INSTRUCBUS[13]; JSR = INSTRUCBUS[14]; LD = INSTRUCBUS[15]; ST = INSTRUCBUS[16];
  //   SUB = INSTRUCBUS[17]; AND = INSTRUCBUS[18]; NOT = INSTRUCBUS[19]; MAR15__0[15:0] = MAR; MDR7__0[7:0] = MDR;
  //   FETCH = PHASEFFBUS[0]; ADDR = PHASEFFBUS[1]; EXEC = PHASEFFBUS[2]; INTR = PHASEFFBUS[3];
  //   PSW15__0 (some bits) = {PSW[15], PSW[4:0]}; PSWSTART = PSW[0]; PSWZ = PSW[1]; PSWN = PSW[2]; PSWV = PSW[3];
  //   PSWC = PSW[4]; PSWI = PSW[15]

  // Notes on the sheet:
  //   ALU
  //   Instrukcijski registar
  //   MAR
  //   Dekoderi za prepoznavanje instrukcije na osnovu sadrzaja IR31..24
  //   Dekoder za prepoznavanje nacina adresiranja na osnovu IR23..16
  //   MDR
  //   Sabiraci za pcrelpom i grananja
  //   Pomocni registar B i ostali pomocni registri
  //   FF za pokretanje FETCH, ADDR, EXEC i INTR faze izvršavanja instrukcije
  //   (OVO JE ACC)
  //   Programska statusna reč (PSW)
  //   PC
  //   SP
  //   A
  //   Registri opste namene
endmodule

module FETCH (
  input  in_1,
  input  in_2,
  input  in_3,
  input  [3:0] PHASEFFBUS,
  input  [19:0] INSTRUCBUS,
  input  [5:0] ADDRBUS,
  input  [15:0] PSW,
  output [14:0] CMEMBUS,
  output [7:0] CFFBUS,
  output [23:0] CREGBUS,
  output rdMEM
);

  wire adr2, adr3, and_3_out, and_4_out, and_5_out, and_6_out, and_7_out, and_8_out, and_9_out, and_10_out,
       and_11_out, and_12_out, and_13_out, bezadr1, bradr2, bradr3, branch2, brbezadr1, brbranch2, brcnd,
       brgrinst, brjmp3, brnotfcmem, bruncnd, clFETCH, grinst, incPC, jmp3, ldIR7__0, ldIR15__8, ldIR23__16,
       ldIR31__24, ldMAR, ldMDR, not_1_out, not_3_out, not_4_out, not_5_out, not_6_out, notPSWSTandFETCH,
       or_4_out, or_5_out, or_7_out, or_8_out, or_9_out, or_11_out, rdMEM_t, reg1_cl_inc_ld_1_p4,
       reg5_cl_inc_ld_1_p5, reg5_cl_inc_ld_1_p6, stADDR, stEXEC;
  wire [3:0] dc4_16_1_p1;
  wire [4:0] reg5_cl_inc_ld_1_p3, reg5_cl_inc_ld_1_p4;
  wire [23:11] rom_1_data;

  or or_1 (branch2, INSTRUCBUS[7], INSTRUCBUS[8], INSTRUCBUS[9], INSTRUCBUS[10]);
  or or_2 (bezadr1, INSTRUCBUS[0], INSTRUCBUS[1], INSTRUCBUS[2], INSTRUCBUS[3], INSTRUCBUS[4], INSTRUCBUS[5], INSTRUCBUS[6]);
  not not_1 (not_1_out, in_1);
  // REG5_CL_INC_LD reg5_cl_inc_ld_1: pin names not known; wires that end beside it: in_2, not_1_out, reg5_cl_inc_ld_1_p3, reg5_cl_inc_ld_1_p4, reg5_cl_inc_ld_1_p5, reg5_cl_inc_ld_1_p6
  not not_2 (reg5_cl_inc_ld_1_p6, reg5_cl_inc_ld_1_p5);
  // DC4_16 dc4_16_1: pin names not known; wires that end beside it: dc4_16_1_p1, 1'b1, bruncnd, notPSWSTandFETCH, brbezadr1, brbranch2, bradr2, brjmp3, bradr3, brnotfcmem, brgrinst
  or or_3 (reg5_cl_inc_ld_1_p5, bruncnd, brcnd);
  or or_4 (or_4_out, INSTRUCBUS[15], INSTRUCBUS[16], INSTRUCBUS[17], INSTRUCBUS[18], INSTRUCBUS[19]);
  or or_5 (or_5_out, ADDRBUS[2], ADDRBUS[4]);
  or or_6 (jmp3, INSTRUCBUS[11], INSTRUCBUS[12], INSTRUCBUS[13], INSTRUCBUS[14]);
  ROM #(.addrWidth(5), .dataWidth(24)) rom_1 (
    .addr(reg5_cl_inc_ld_1_p4),
    .data({rom_1_data[23:21], reg5_cl_inc_ld_1_p3, dc4_16_1_p1, rom_1_data[11], stEXEC, stADDR, clFETCH, ldIR7__0, ldIR15__8, ldIR23__16, ldIR31__24, ldMDR, rdMEM_t, incPC, ldMAR}),
    .sel(1'b1));
  and and_1 (adr2, or_4_out, or_5_out);
  or or_7 (or_7_out, INSTRUCBUS[15], INSTRUCBUS[16], INSTRUCBUS[17], INSTRUCBUS[18], INSTRUCBUS[19]);
  and and_2 (adr3, or_7_out, ADDRBUS[5]);
  not not_3 (not_3_out, PHASEFFBUS[0]);
  not not_4 (not_4_out, PSW[0]);
  or or_8 (or_8_out, not_3_out, not_4_out);
  not not_5 (not_5_out, in_3);
  and and_3 (and_3_out, or_8_out, notPSWSTandFETCH);
  and and_4 (and_4_out, brbezadr1, bezadr1);
  and and_5 (and_5_out, brbranch2, branch2);
  and and_6 (and_6_out, bradr2, adr2);
  and and_7 (and_7_out, brjmp3, jmp3);
  and and_8 (and_8_out, bradr3, adr3);
  and and_9 (and_9_out, brnotfcmem, not_5_out);
  and and_10 (and_10_out, brgrinst, grinst);
  or or_9 (or_9_out, INSTRUCBUS[0], INSTRUCBUS[1], INSTRUCBUS[2], INSTRUCBUS[3], INSTRUCBUS[4], INSTRUCBUS[5], INSTRUCBUS[6], INSTRUCBUS[7], INSTRUCBUS[8], INSTRUCBUS[9], INSTRUCBUS[10], INSTRUCBUS[11], INSTRUCBUS[12], INSTRUCBUS[13], INSTRUCBUS[14], INSTRUCBUS[15], INSTRUCBUS[16], INSTRUCBUS[17], INSTRUCBUS[18], INSTRUCBUS[19]);
  not not_6 (not_6_out, or_9_out);
  and and_11 (and_11_out, INSTRUCBUS[16], reg1_cl_inc_ld_1_p4, ADDRBUS[0]);
  or or_10 (brcnd, and_3_out, and_4_out, and_5_out, and_6_out, and_7_out, and_8_out, and_9_out, and_10_out);
  // REG1_CL_INC_LD reg1_cl_inc_ld_1: pin names not known; wires that end beside it: clFETCH, in_2, 1'b0, reg1_cl_inc_ld_1_p4, ldIR31__24, ldIR23__16
  and and_12 (and_12_out, ~ADDRBUS[0], ~ADDRBUS[1], ~ADDRBUS[2], ~ADDRBUS[3], ~ADDRBUS[4], ~ADDRBUS[5]);  // AND_Gate
  or or_11 (or_11_out, INSTRUCBUS[15], INSTRUCBUS[16], INSTRUCBUS[17], INSTRUCBUS[18], INSTRUCBUS[19]);
  and and_13 (and_13_out, and_12_out, reg1_cl_inc_ld_1_p4, or_11_out);
  or or_12 (grinst, and_11_out, not_6_out, and_13_out);
  assign CREGBUS[4] = ldIR7__0 ? 1'b1 : 1'bz;  // Controlled_Buffer controlled_buffer_1
  assign CREGBUS[5] = ldIR15__8 ? 1'b1 : 1'bz;  // Controlled_Buffer controlled_buffer_2
  assign CREGBUS[6] = ldIR23__16 ? 1'b1 : 1'bz;  // Controlled_Buffer controlled_buffer_3
  assign CREGBUS[7] = ldIR31__24 ? 1'b1 : 1'bz;  // Controlled_Buffer controlled_buffer_4
  assign CMEMBUS[0] = ldMAR ? 1'b1 : 1'bz;  // Controlled_Buffer controlled_buffer_5
  assign CMEMBUS[2] = ldMDR ? 1'b1 : 1'bz;  // Controlled_Buffer controlled_buffer_6
  assign CMEMBUS[4] = incPC ? 1'b1 : 1'bz;  // Controlled_Buffer controlled_buffer_7
  assign CFFBUS[1] = clFETCH ? 1'b1 : 1'bz;  // Controlled_Buffer controlled_buffer_8
  assign CFFBUS[2] = stADDR ? 1'b1 : 1'bz;  // Controlled_Buffer controlled_buffer_9
  assign CFFBUS[4] = stEXEC ? 1'b1 : 1'bz;  // Controlled_Buffer controlled_buffer_10
  assign rdMEM = rdMEM_t ? 1'b1 : 1'bz;  // Controlled_Buffer controlled_buffer_11

  // Other names for the same wires on the sheet: immed = ADDRBUS[0]; memdir = ADDRBUS[1]; regdir = ADDRBUS[2];
  //   memind = ADDRBUS[3]; postincr = ADDRBUS[4]; pcrelpom = ADDRBUS[5]; CLK = in_2; FCBUS = in_3;
  //   HALT = INSTRUCBUS[0]; RTS = INSTRUCBUS[1]; RTI = INSTRUCBUS[2]; ASL = INSTRUCBUS[3]; ROLC = INSTRUCBUS[4];
  //   PUSHGPR = INSTRUCBUS[5]; POPGPR = INSTRUCBUS[6]; BLSS = INSTRUCBUS[7]; BNCR = INSTRUCBUS[8];
  //   BGRTU = INSTRUCBUS[9]; BNEG = INSTRUCBUS[10]; JLEQ = INSTRUCBUS[11]; LOOPGRE = INSTRUCBUS[12];
  //   JMP = INSTRUCBUS[13]; JSR = INSTRUCBUS[14]; LD = INSTRUCBUS[15]; ST = INSTRUCBUS[16]; SUB = INSTRUCBUS[17];
  //   AND = INSTRUCBUS[18]; NOT = INSTRUCBUS[19]; FETCH = PHASEFFBUS[0]; ADDR = PHASEFFBUS[1]; EXEC = PHASEFFBUS[2];
  //   INTR = PHASEFFBUS[3]; PSWSTART = PSW[0]; rst = in_1

  // Notes on the sheet:
  //   Operaciona jedinica
  //   Kontrolna jedinica
  //   contents of rom_1 (hex, n*v repeats v):
  //   2000 3 2800c 10 9000 133000 3 7800c 134020 9000 125000 3 c800c 136040 127000 3 10800c 80 1300 1500
endmodule

module ADDR (
  input  in_1,
  input  in_2,
  input  in_3,
  input  [3:0] PHASEFFBUS,
  input  [19:0] INSTRUCBUS,
  input  [5:0] ADDRBUS,
  output [14:0] CMEMBUS,
  output [7:0] CFFBUS,
  output [23:0] CREGBUS,
  output rdMEM
);

  wire and_1_out, and_2_out, and_3_out, bradr, brcnd, brnotADDR, brnotFCBUS, brST, bruncnd, clADDR, incB,
       incMAR, ldB, ldDWH, ldDWL, ldMAR, ldMDR, mxB0, mxB1, mxGPRADR0, mxMAR0, mxMAR1, not_1_out, not_3_out,
       not_4_out, rdMEM_t, reg5_cl_inc_ld_1_p5, reg5_cl_inc_ld_1_p6, stEXEC, wrGPR;
  wire [2:0] dc3_8_1_p1;
  wire [4:0] kmadr_1_adr3__0, multiplexer_1_out, reg5_cl_inc_ld_1_p4, rom_1_data;

  not not_1 (not_1_out, in_1);
  // DC3_8 dc3_8_1: pin names not known; wires that end beside it: dc3_8_1_p1, 1'b1, bruncnd, brnotADDR, brST, brnotFCBUS, bradr
  KMADR kmadr_1 (
    .immed(ADDRBUS[0]), .memdir(ADDRBUS[1]), .regdir(ADDRBUS[2]), .memind(ADDRBUS[3]),
    .Adr3__0(kmadr_1_adr3__0), .postincr(ADDRBUS[4]), .pcrelpom(ADDRBUS[5]));
  Multiplexer #(.width(5), .enable("false")) multiplexer_1 (
    .in0(rom_1_data), .in1(kmadr_1_adr3__0), .out(multiplexer_1_out), .sel(bradr));
  // REG5_CL_INC_LD reg5_cl_inc_ld_1: pin names not known; wires that end beside it: in_2, not_1_out, multiplexer_1_out, reg5_cl_inc_ld_1_p4, reg5_cl_inc_ld_1_p5, reg5_cl_inc_ld_1_p6
  not not_2 (reg5_cl_inc_ld_1_p6, reg5_cl_inc_ld_1_p5);
  or or_1 (reg5_cl_inc_ld_1_p5, bruncnd, bradr, brcnd);
  ROM #(.addrWidth(5), .dataWidth(24)) rom_1 (
    .addr(reg5_cl_inc_ld_1_p4),
    .data({rom_1_data, dc3_8_1_p1, mxGPRADR0, stEXEC, clADDR, wrGPR, incB, mxMAR1, mxB1, ldDWH, incMAR, ldDWL, rdMEM_t, ldMDR, mxMAR0, ldMAR, mxB0, ldB}),
    .sel(1'b1));
  not not_3 (not_3_out, PHASEFFBUS[1]);
  and and_1 (and_1_out, not_3_out, brnotADDR);
  and and_2 (and_2_out, INSTRUCBUS[16], brST);
  not not_4 (not_4_out, in_3);
  and and_3 (and_3_out, brnotFCBUS, not_4_out);
  or or_2 (brcnd, and_1_out, and_2_out, and_3_out);
  assign CMEMBUS[0] = ldMAR ? 1'b1 : 1'bz;  // Controlled_Buffer controlled_buffer_1
  assign CMEMBUS[1] = incMAR ? 1'b1 : 1'bz;  // Controlled_Buffer controlled_buffer_2
  assign CMEMBUS[2] = ldMDR ? 1'b1 : 1'bz;  // Controlled_Buffer controlled_buffer_3
  assign CMEMBUS[5] = mxMAR0 ? 1'b1 : 1'bz;  // Controlled_Buffer controlled_buffer_4
  assign CMEMBUS[6] = mxMAR1 ? 1'b1 : 1'bz;  // Controlled_Buffer controlled_buffer_5
  assign CFFBUS[3] = clADDR ? 1'b1 : 1'bz;  // Controlled_Buffer controlled_buffer_6
  assign CFFBUS[4] = stEXEC ? 1'b1 : 1'bz;  // Controlled_Buffer controlled_buffer_7
  assign CREGBUS[0] = ldB ? 1'b1 : 1'bz;  // Controlled_Buffer controlled_buffer_8
  assign CREGBUS[1] = mxB0 ? 1'b1 : 1'bz;  // Controlled_Buffer controlled_buffer_9
  assign CREGBUS[2] = mxB1 ? 1'b1 : 1'bz;  // Controlled_Buffer controlled_buffer_10
  assign CREGBUS[3] = wrGPR ? 1'b1 : 1'bz;  // Controlled_Buffer controlled_buffer_11
  assign CREGBUS[8] = ldDWH ? 1'b1 : 1'bz;  // Controlled_Buffer controlled_buffer_12
  assign CREGBUS[9] = ldDWL ? 1'b1 : 1'bz;  // Controlled_Buffer controlled_buffer_13
  assign CREGBUS[10] = incB ? 1'b1 : 1'bz;  // Controlled_Buffer controlled_buffer_14
  assign CREGBUS[11] = mxGPRADR0 ? 1'b1 : 1'bz;  // Controlled_Buffer controlled_buffer_15
  assign rdMEM = rdMEM_t ? 1'b1 : 1'bz;  // Controlled_Buffer controlled_buffer_16

  // Other names for the same wires on the sheet: immed = ADDRBUS[0]; memdir = ADDRBUS[1]; regdir = ADDRBUS[2];
  //   memind = ADDRBUS[3]; postincr = ADDRBUS[4]; pcrelpom = ADDRBUS[5]; CLK = in_2; FCBUS = in_3;
  //   HALT = INSTRUCBUS[0]; RTS = INSTRUCBUS[1]; RTI = INSTRUCBUS[2]; ASL = INSTRUCBUS[3]; ROLC = INSTRUCBUS[4];
  //   PUSHGPR = INSTRUCBUS[5]; POPGPR = INSTRUCBUS[6]; BLSS = INSTRUCBUS[7]; BNCR = INSTRUCBUS[8];
  //   BGRTU = INSTRUCBUS[9]; BNEG = INSTRUCBUS[10]; JLEQ = INSTRUCBUS[11]; LOOPGRE = INSTRUCBUS[12];
  //   JMP = INSTRUCBUS[13]; JSR = INSTRUCBUS[14]; LD = INSTRUCBUS[15]; ST = INSTRUCBUS[16]; SUB = INSTRUCBUS[17];
  //   AND = INSTRUCBUS[18]; NOT = INSTRUCBUS[19]; FETCH = PHASEFFBUS[0]; ADDR = PHASEFFBUS[1]; EXEC = PHASEFFBUS[2];
  //   INTR = PHASEFFBUS[3]; rst = in_1

  // Notes on the sheet:
  //   Operaciona jedinica
  //   Upravljacka jedinica
  //   contents of rom_1 (hex, n*v repeats v):
  //   20000 50000 c10003 91000c c30000 c18001 c 3c0030 c0 4c0030 100 201 91040c 8005 800 800 919000 404
  //   c30000 9c0030 c0 ac0030 100 201 16000
endmodule

module EXEC (
  input  in_1,
  input  in_2,
  input  in_3,
  input  [15:0] B,
  input  [3:0] PHASEFFBUS,
  input  [19:0] INSTRUCBUS,
  input  [5:0] ADDRBUS,
  input  [15:0] PSW,
  output [7:0] A,
  output [7:0] ALU,
  output [14:0] CMEMBUS,
  output [7:0] CFFBUS,
  output [23:0] CREGBUS,
  output rdMEM,
  output wrMEM,
  output [6:0] CPSW
);

  wire and_1_out, and_2_out, and_3_out, and_4_out, and_5_out, and_6_out, and_9_out, and_10_out, and_11_out,
       and_12_out, and_13_out, and_14_out, ANDALU, brcnd, brnotbrorjmp, brnotEXEC, brnotFCBUS, brnotifbeq0,
       brnotifbeq15, bropr, brorjmp, brregdir, bruncnd, clEXEC, clPSWSTART, decB, decSP, IFBEQ0, IFBEQ15,
       incB, incMAR, incSP, ldB, ldC, ldDWH, ldDWL, ldI, ldMAR, ldMDR, ldN, ldPC, ldSTART, ldV, ldZ,
       mp2_8b_1_p3, mxB0, mxB1, mxGPRADR0, mxGPRADR1, mxGPRADR2, mxGPRIN0, mxGPRIN1, mxGPRIN2, mxMDR0,
       mxMDR1, not_1_out, not_2_out, not_3_out, not_4_out, NOTALU, or_1_out, or_2_out, rdMEM_t,
       reg8_inc_ld_1_p5, reg8_inc_ld_1_p6, slB, stINTR, SUBALU, wrGPR, wrMEM_t, xor_1_out;
  wire [6:0] kmopr_1_adr6__0, reg8_inc_ld_1_p4;
  wire [7:7] reg8_inc_ld_1_p4_2;
  wire [19:6] dc4_16_1_p1;
  wire [28:28] rom_2_data;

  xor xor_1 (xor_1_out, PSW[2], PSW[3]);
  and and_1 (and_1_out, INSTRUCBUS[12], not_1_out);
  not not_1 (not_1_out, xor_1_out);
  and and_2 (and_2_out, xor_1_out, INSTRUCBUS[7]);
  or or_1 (or_1_out, xor_1_out, PSW[1]);
  not not_2 (not_2_out, PSW[4]);
  and and_3 (and_3_out, not_2_out, INSTRUCBUS[8]);
  or or_2 (or_2_out, PSW[4], PSW[1]);
  and and_4 (and_4_out, PSW[2], INSTRUCBUS[10]);
  and and_5 (and_5_out, or_1_out, INSTRUCBUS[11]);
  not not_3 (not_3_out, or_2_out);
  and and_6 (and_6_out, not_3_out, INSTRUCBUS[9]);
  // DC4_16 dc4_16_1: pin names not known; wires that end beside it: dc4_16_1_p1[9:6], 1'b1, bruncnd, brnotEXEC, brregdir, brnotFCBUS, brnotbrorjmp, brnotifbeq15, brnotifbeq0, bropr
  or or_3 (brorjmp, and_1_out, and_2_out, and_5_out, and_3_out, and_6_out, and_4_out);
  not not_4 (not_4_out, in_1);
  KMOPR kmopr_1 (
    .LD(INSTRUCBUS[15]), .ST(INSTRUCBUS[16]), .SUB(INSTRUCBUS[17]), .AND(INSTRUCBUS[18]),
    .NOT(INSTRUCBUS[19]), .BLSS(INSTRUCBUS[7]), .JLEQ(INSTRUCBUS[11]), .LOOPGRE(INSTRUCBUS[12]),
    .JMP(INSTRUCBUS[13]), .JSR(INSTRUCBUS[14]), .ASL(INSTRUCBUS[3]), .Adr6__0(kmopr_1_adr6__0),
    .BNCR(INSTRUCBUS[8]), .BGRTU(INSTRUCBUS[9]), .BNEG(INSTRUCBUS[10]), .RTS(INSTRUCBUS[1]),
    .RTI(INSTRUCBUS[2]), .PUSHGPR(INSTRUCBUS[5]), .POPGPR(INSTRUCBUS[6]), .ROLC(INSTRUCBUS[4]),
    .HALT(INSTRUCBUS[0]));
  // MP2_8b mp2_8b_1: pin names not known; wires that end beside it: bropr, {1'b0, dc4_16_1_p1[16:10]}, mp2_8b_1_p3, {1'b0, kmopr_1_adr6__0}, 1'b1
  // REG8_INC_LD reg8_inc_ld_1: pin names not known; wires that end beside it: in_2, not_4_out, mp2_8b_1_p3, {reg8_inc_ld_1_p4_2[7], reg8_inc_ld_1_p4}, reg8_inc_ld_1_p5, reg8_inc_ld_1_p6
  ROM #(.addrWidth(7), .dataWidth(20)) rom_1 (
    .addr(reg8_inc_ld_1_p4), .data({dc4_16_1_p1, clEXEC, stINTR, clPSWSTART, incB, mxGPRADR2, mxB0}),
    .sel(1'b1));
  or or_4 (reg8_inc_ld_1_p5, bruncnd, brcnd, bropr);
  not not_5 (reg8_inc_ld_1_p6, reg8_inc_ld_1_p5);
  ROM #(.addrWidth(7), .dataWidth(32)) rom_2 (
    .addr(reg8_inc_ld_1_p4),
    .data({mxB1, ldI, ldSTART, rom_2_data[28], ldDWH, ldDWL, rdMEM_t, incSP, slB, ldMAR, decSP, mxGPRIN1, decB, mxGPRIN0, ldPC, NOTALU, mxGPRIN2, ANDALU, ldC, ldV, SUBALU, ldB, incMAR, mxMDR0, wrMEM_t, mxMDR1, ldMDR, ldZ, ldN, mxGPRADR1, mxGPRADR0, wrGPR}),
    .sel(1'b1));
  and and_7 (IFBEQ15, B[0], B[1], B[2], B[3]);
  and and_8 (IFBEQ0, ~B[0], ~B[1], ~B[2], ~B[3]);  // AND_Gate
  and and_9 (and_9_out, brnotEXEC, ~PHASEFFBUS[2]);  // AND_Gate
  and and_10 (and_10_out, brregdir, ADDRBUS[2]);
  and and_11 (and_11_out, brnotFCBUS, ~in_3);  // AND_Gate
  and and_12 (and_12_out, brnotbrorjmp, ~brorjmp);  // AND_Gate
  and and_13 (and_13_out, brnotifbeq15, ~IFBEQ15);  // AND_Gate
  and and_14 (and_14_out, brnotifbeq0, ~IFBEQ0);  // AND_Gate
  or or_5 (brcnd, and_9_out, and_10_out, and_11_out, and_12_out, and_13_out, and_14_out);
  assign CMEMBUS[0] = ldMAR ? 1'b1 : 1'bz;  // Controlled_Buffer controlled_buffer_1
  assign CMEMBUS[1] = incMAR ? 1'b1 : 1'bz;  // Controlled_Buffer controlled_buffer_2
  assign CMEMBUS[2] = ldMDR ? 1'b1 : 1'bz;  // Controlled_Buffer controlled_buffer_3
  assign CMEMBUS[3] = ldPC ? 1'b1 : 1'bz;  // Controlled_Buffer controlled_buffer_4
  assign CMEMBUS[8] = mxMDR0 ? 1'b1 : 1'bz;  // Controlled_Buffer controlled_buffer_5
  assign CMEMBUS[9] = mxMDR1 ? 1'b1 : 1'bz;  // Controlled_Buffer controlled_buffer_6
  assign CMEMBUS[11] = incSP ? 1'b1 : 1'bz;  // Controlled_Buffer controlled_buffer_7
  assign CMEMBUS[12] = decSP ? 1'b1 : 1'bz;  // Controlled_Buffer controlled_buffer_8
  assign CREGBUS[0] = ldB ? 1'b1 : 1'bz;  // Controlled_Buffer controlled_buffer_9
  assign CREGBUS[1] = mxB0 ? 1'b1 : 1'bz;  // Controlled_Buffer controlled_buffer_10
  assign CREGBUS[2] = mxB1 ? 1'b1 : 1'bz;  // Controlled_Buffer controlled_buffer_11
  assign CREGBUS[3] = wrGPR ? 1'b1 : 1'bz;  // Controlled_Buffer controlled_buffer_12
  assign CREGBUS[8] = ldDWH ? 1'b1 : 1'bz;  // Controlled_Buffer controlled_buffer_13
  assign CREGBUS[9] = ldDWL ? 1'b1 : 1'bz;  // Controlled_Buffer controlled_buffer_14
  assign CREGBUS[10] = incB ? 1'b1 : 1'bz;  // Controlled_Buffer controlled_buffer_15
  assign CREGBUS[11] = mxGPRADR0 ? 1'b1 : 1'bz;  // Controlled_Buffer controlled_buffer_16
  assign CREGBUS[12] = mxGPRADR1 ? 1'b1 : 1'bz;  // Controlled_Buffer controlled_buffer_17
  assign CREGBUS[13] = mxGPRIN0 ? 1'b1 : 1'bz;  // Controlled_Buffer controlled_buffer_18
  assign CREGBUS[14] = mxGPRIN1 ? 1'b1 : 1'bz;  // Controlled_Buffer controlled_buffer_19
  assign CREGBUS[15] = mxGPRIN2 ? 1'b1 : 1'bz;  // Controlled_Buffer controlled_buffer_20
  assign CREGBUS[16] = slB ? 1'b1 : 1'bz;  // Controlled_Buffer controlled_buffer_21
  assign CREGBUS[17] = decB ? 1'b1 : 1'bz;  // Controlled_Buffer controlled_buffer_22
  assign CPSW[0] = clPSWSTART ? 1'b1 : 1'bz;  // Controlled_Buffer controlled_buffer_23
  assign CPSW[1] = ldSTART ? 1'b1 : 1'bz;  // Controlled_Buffer controlled_buffer_24
  assign CPSW[2] = ldZ ? 1'b1 : 1'bz;  // Controlled_Buffer controlled_buffer_25
  assign CPSW[3] = ldN ? 1'b1 : 1'bz;  // Controlled_Buffer controlled_buffer_26
  assign CPSW[4] = ldV ? 1'b1 : 1'bz;  // Controlled_Buffer controlled_buffer_27
  assign CPSW[5] = ldC ? 1'b1 : 1'bz;  // Controlled_Buffer controlled_buffer_28
  assign CPSW[6] = ldI ? 1'b1 : 1'bz;  // Controlled_Buffer controlled_buffer_29
  assign CFFBUS[5] = clEXEC ? 1'b1 : 1'bz;  // Controlled_Buffer controlled_buffer_30
  assign CFFBUS[6] = stINTR ? 1'b1 : 1'bz;  // Controlled_Buffer controlled_buffer_31
  assign CREGBUS[18] = mxGPRADR2 ? 1'b1 : 1'bz;  // Controlled_Buffer controlled_buffer_32
  assign CREGBUS[19] = NOTALU ? 1'b1 : 1'bz;  // Controlled_Buffer controlled_buffer_33
  assign CREGBUS[20] = SUBALU ? 1'b1 : 1'bz;  // Controlled_Buffer controlled_buffer_34
  assign CREGBUS[21] = ANDALU ? 1'b1 : 1'bz;  // Controlled_Buffer controlled_buffer_35
  assign rdMEM = rdMEM_t ? 1'b1 : 1'bz;  // Controlled_Buffer controlled_buffer_36
  assign wrMEM = wrMEM_t ? 1'b1 : 1'bz;  // Controlled_Buffer controlled_buffer_37

  // Other names for the same wires on the sheet: A7__0[7:0] = A; immed = ADDRBUS[0]; regdir = ADDRBUS[2];
  //   ALU7__0[7:0] = ALU; B15__0[15:0] = B; CLK = in_2; FCBUS = in_3; HALT = INSTRUCBUS[0]; RTS = INSTRUCBUS[1];
  //   RTI = INSTRUCBUS[2]; ASL = INSTRUCBUS[3]; ROLC = INSTRUCBUS[4]; PUSHGPR = INSTRUCBUS[5]; POPGPR = INSTRUCBUS[6];
  //   BLSS = INSTRUCBUS[7]; BNCR = INSTRUCBUS[8]; BGRTU = INSTRUCBUS[9]; BNEG = INSTRUCBUS[10]; JLEQ = INSTRUCBUS[11];
  //   LOOPGRE = INSTRUCBUS[12]; JMP = INSTRUCBUS[13]; JSR = INSTRUCBUS[14]; LD = INSTRUCBUS[15]; ST = INSTRUCBUS[16];
  //   SUB = INSTRUCBUS[17]; AND = INSTRUCBUS[18]; NOT = INSTRUCBUS[19]; EXEC = PHASEFFBUS[2]; PSWSTART = PSW[0];
  //   PSWZ = PSW[1]; PSWN = PSW[2]; PSWV = PSW[3]; PSWC = PSW[4]; PSWI = PSW[15]; rst = in_1

  // Notes on the sheet:
  //   Operaciona jedinica
  //   Upravljacka jedinica
  //   51-32
  //   contents of rom_1 (hex, n*v repeats v):
  //   80 200 0 14440 28c0 0 1900 0 2100 14440 0 14440 0 14440 0 14440 0 14440 14540 14440 14540 6c40 14540
  //   4*0 14440 0 0 0 7d00 0 0 0 8d00 14440 0 0 0 14440 0 a900 0 b100 0 14440 0 c100 0 c900 0 0 0 d900 0
  //   e100 0 0 a440 1 0 0 2 10100 0 0 2 11100 f584 14440 1 0 12500 0 0 13100 0 121c2 14440 8 70
  //   31-0
  //   contents of rom_2 (hex, n*v repeats v):
  //   0 0 7 1e 0 66 80 326 80 0 406 3 b807 1e c007 1e 18007 1e 0 60000 0 0 0 406 82000 1007 1e 120000
  //   200004 120 400004 80 200004 60 400004 80 120000 406 802000 7 1e 1400004 2000020 5400004 2000020
  //   8000000 160000 1400004 2000020 5400004 2000020 8000000 60003018 1400004 2000020 5400004 2000020
  //   8000000 80000400 7 80000400 200004 400004 120 80 200004 400004 60 80 0 0 80000400 1400004 2000020
  //   4000000 1400004 2000020 8000000 1c0001
endmodule

module INTR (
  input  in_1,
  input  in_2,
  input  in_3,
  input  [3:0] PHASEFFBUS,
  input  [19:0] INSTRUCBUS,
  input  [15:0] PSW,
  input  [3:0] intr,
  output [15:0] ADDIVTP,
  output [1:0] UEXT1__0,
  output inta,
  output [14:0] CMEMBUS,
  output [7:0] CFFBUS,
  output [23:0] CREGBUS,
  output rdMEM,
  output wrMEM
);

  wire and_2_out, and_3_out, and_4_out, brcnd, brnotFCBUS, brnotINTR, brnotprekid, bruncnd, clINTR, decSP,
       incMAR, ldDWH, ldDWL, ldMAR, ldMDR, ldPC, mxGPRADR0, mxGPRADR1, mxGPRIN0, mxGPRIN1, mxMAR2, mxMDR0,
       mxMDR1, mxMDR2, not_1_out, not_3_out, not_4_out, not_5_out, not_6_out, not_7_out, prekid, prper,
       rdMEM_t, reg5_cl_inc_ld_1_p5, reg5_cl_inc_ld_1_p6, stFETCH, wrMEM_t;
  wire [2:0] dc3_8_1_p1;
  wire [2:1] IVTDSP15__0;
  wire [4:0] reg5_cl_inc_ld_1_p3, reg5_cl_inc_ld_1_p4;
  wire [15:0] IVTP15__0;

  // DC3_8 dc3_8_1: pin names not known; wires that end beside it: dc3_8_1_p1, 1'b1, bruncnd, brnotINTR, brnotprekid, brnotFCBUS
  not not_1 (not_1_out, in_1);
  // REG5_CL_INC_LD reg5_cl_inc_ld_1: pin names not known; wires that end beside it: in_2, not_1_out, reg5_cl_inc_ld_1_p3, reg5_cl_inc_ld_1_p4, reg5_cl_inc_ld_1_p5, reg5_cl_inc_ld_1_p6
  not not_2 (reg5_cl_inc_ld_1_p6, reg5_cl_inc_ld_1_p5);
  or or_1 (reg5_cl_inc_ld_1_p5, bruncnd, brcnd);
  ROM #(.addrWidth(5), .dataWidth(28)) rom_1 (
    .addr(reg5_cl_inc_ld_1_p4),
    .data({reg5_cl_inc_ld_1_p3, dc3_8_1_p1, clINTR, stFETCH, ldPC, mxGPRIN1, mxGPRIN0, ldDWH, ldDWL, incMAR, rdMEM_t, mxMAR2, inta, mxMDR2, mxGPRADR0, wrMEM_t, mxMDR1, ldMAR, mxMDR0, ldMDR, mxGPRADR1, decSP}),
    .sel(1'b1));
  and and_1 (prekid, prper, 1'b1, not_3_out);
  not not_3 (not_3_out, INSTRUCBUS[0]);
  not not_4 (not_4_out, in_1);
  or or_2 (prper, intr[3], intr[2], intr[1], intr[0]);
  // REG16_LD reg16_ld_1: pin names not known; wires that end beside it: in_2, not_4_out, IVTP15__0, PSW[15]
  // CD4 cd4_1: pin names not known; wires that end beside it: intr[3], intr[2], intr[1], intr[0], 1'b1, UEXT1__0[1], UEXT1__0[0]
  // REG2_LD reg2_ld_1: pin names not known; wires that end beside it: in_2, UEXT1__0, IVTDSP15__0, inta
  not not_5 (not_5_out, PHASEFFBUS[3]);
  not not_6 (not_6_out, prekid);
  not not_7 (not_7_out, in_3);
  and and_2 (and_2_out, brnotINTR, not_5_out);
  and and_3 (and_3_out, brnotprekid, not_6_out);
  and and_4 (and_4_out, brnotFCBUS, not_7_out);
  // ADD16 add16_1: pin names not known; wires that end beside it: IVTP15__0, ADDIVTP, {{13{1'b0}}, IVTDSP15__0, 1'b0}, 1'b0
  or or_3 (brcnd, and_2_out, and_3_out, and_4_out);
  assign CMEMBUS[0] = ldMAR ? 1'b1 : 1'bz;  // Controlled_Buffer controlled_buffer_1
  assign CMEMBUS[1] = incMAR ? 1'b1 : 1'bz;  // Controlled_Buffer controlled_buffer_2
  assign CMEMBUS[2] = ldMDR ? 1'b1 : 1'bz;  // Controlled_Buffer controlled_buffer_3
  assign CMEMBUS[3] = ldPC ? 1'b1 : 1'bz;  // Controlled_Buffer controlled_buffer_4
  assign CMEMBUS[7] = mxMAR2 ? 1'b1 : 1'bz;  // Controlled_Buffer controlled_buffer_5
  assign CMEMBUS[8] = mxMDR0 ? 1'b1 : 1'bz;  // Controlled_Buffer controlled_buffer_6
  assign CMEMBUS[9] = mxMDR1 ? 1'b1 : 1'bz;  // Controlled_Buffer controlled_buffer_7
  assign CMEMBUS[10] = mxMDR2 ? 1'b1 : 1'bz;  // Controlled_Buffer controlled_buffer_8
  assign CMEMBUS[12] = decSP ? 1'b1 : 1'bz;  // Controlled_Buffer controlled_buffer_9
  assign CREGBUS[8] = ldDWH ? 1'b1 : 1'bz;  // Controlled_Buffer controlled_buffer_10
  assign CREGBUS[9] = ldDWL ? 1'b1 : 1'bz;  // Controlled_Buffer controlled_buffer_11
  assign CREGBUS[11] = mxGPRADR0 ? 1'b1 : 1'bz;  // Controlled_Buffer controlled_buffer_12
  assign CREGBUS[12] = mxGPRADR1 ? 1'b1 : 1'bz;  // Controlled_Buffer controlled_buffer_13
  assign CFFBUS[0] = stFETCH ? 1'b1 : 1'bz;  // Controlled_Buffer controlled_buffer_14
  assign CFFBUS[7] = clINTR ? 1'b1 : 1'bz;  // Controlled_Buffer controlled_buffer_15
  assign CREGBUS[13] = mxGPRIN0 ? 1'b1 : 1'bz;  // Controlled_Buffer controlled_buffer_16
  assign CREGBUS[14] = mxGPRIN1 ? 1'b1 : 1'bz;  // Controlled_Buffer controlled_buffer_17
  assign rdMEM = rdMEM_t ? 1'b1 : 1'bz;  // Controlled_Buffer controlled_buffer_18
  assign wrMEM = wrMEM_t ? 1'b1 : 1'bz;  // Controlled_Buffer controlled_buffer_19

  // Other names for the same wires on the sheet: ldBR = inta; ADDIVTP15__0[15:0] = ADDIVTP; CLK = in_2; FCBUS = in_3;
  //   HALT = INSTRUCBUS[0]; intr3__0[3:0] = intr; INTR_t = PHASEFFBUS[3]; PSWI = PSW[15]; rst = in_1

  // Notes on the sheet:
  //   Operaciona jedinica
  //   Upravljacka jedinica
  //   contents of rom_1 (hex, n*v repeats v):
  //   200000 fb00000 3 c 12 2c00040 3 24 12 4c00040 3 12 8e 6c00040 3 12 a6 8c00040 3 3e a400040 3 116
  //   bc00040 200 410 d400804 3000 e400804 4000 38000 1c0000
endmodule

module RAM (
  input  [15:0] in_1,
  input  in_2,
  input  [7:0] in_3,
  input  in_4,
  input  in_5,
  input  in_6,
  output [7:0] out_7,
  output out_8
);

  wire and_1_out, and_2_out, CNT0, LDCNT, not_1_out, notCNT0, or_1_out, reg4_ld_sl_sr_1_p6, rsff_2_p4,
       rsff_2_p5, rsff_3_p4, sl;
  wire [3:0] CNT, LFSR;

  // RSFF rsff_1: pin names not known; wires that end beside it: 1'b0, in_2, in_6, sl
  or or_1 (or_1_out, in_4, in_5);
  // REG4_LD_SL_SR reg4_ld_sl_sr_1: pin names not known; wires that end beside it: 1'b0, 1'b0, in_2, 4'b1111, LFSR, reg4_ld_sl_sr_1_p6, sl, in_6
  // RisingEdge risingedge_1: pin names not known; wires that end beside it: or_1_out, in_2, LDCNT
  // MEM64Kx8 mem64kx8_1: pin names not known; wires that end beside it: in_1, 1'b1, in_2, in_3, out_7, in_4
  xor xor_1 (reg4_ld_sl_sr_1_p6, LFSR[2], LFSR[3]);
  and and_1 (and_1_out, CNT0, not_1_out);
  not not_1 (not_1_out, LDCNT);
  // RSFF rsff_2: pin names not known; wires that end beside it: and_1_out, in_2, LDCNT, rsff_2_p4, rsff_2_p5
  not not_2 (rsff_2_p4, in_6);
  and and_2 (and_2_out, rsff_2_p5, CNT0);
  // REG4m_DEC_LD reg4m_dec_ld_1: pin names not known; wires that end beside it: in_2, LFSR, CNT, LDCNT, notCNT0, notCNT0
  or or_2 (notCNT0, CNT[0], CNT[1], CNT[2], CNT[3]);
  // RSFF rsff_3: pin names not known; wires that end beside it: out_8, in_2, and_2_out, rsff_3_p4, out_8
  not not_3 (rsff_3_p4, in_6);
  not not_4 (CNT0, notCNT0);

  // Other names for the same wires on the sheet: ADR[15:0] = in_1; CLK = in_2; DIN[7:0] = in_3; DOUT[7:0] = out_7;
  //   fc = out_8; RDMEM = in_5; rst = in_6; WRMEM = in_4

  // Notes on the sheet:
  //   Random broj predstavlja vreme pristupa memoriji
  //   Brojac za generisanje random broja 
  //   Jedinica za generisanje function complete (fc) signala
  //   Brojac za dekrementiranje random broja
endmodule
